# Fritzing sketch light (saved by Fritzing 0.9.3b)
breadboards: 1

parts:
  Part1 = Arduino Uno (Rev3)
  U1 = RF-LINK_TX [package=rf-link_tx]
  S1 = Pushbutton [package="[THT]"]
  S2 = Pushbutton [package="[THT]"]
  R1 = Resistor [tolerance=±5% resistance=10k package=THT]
  R2 = Resistor [tolerance=±5% resistance=10k package=THT]

nets:
  N1: Part1.D10_PWM/SS, S1.Pin_3, S1.Pin_4, R2.Pin_1
  N2: Part1.D11_PWM/MOSI, S2.Pin_3, S2.Pin_4, R1.Pin_1
  N3: Part1.D3_PWM, U1.GND
  N4: Part1.D4, U1.DATA
  N5: Part1.D5_PWM, U1.+5V
  N6: Part1.5V, S1.Pin_1, S1.Pin_2, S2.Pin_1, S2.Pin_2
  N7: Part1.GND, R1.Pin_0, R2.Pin_0
